// Digital circuit 1-bit_memory_cell_(D-flip-flop).dig as structural Verilog
module _1_bit_memory_cell__D_flip_flop (
  input  D,
  input  Clock,
  output Q
);

  wire nand_1_out, nand_2_out, nand_4_out, not_1_out;

  not not_1 (not_1_out, D);
  nand nand_1 (nand_1_out, D, Clock);
  nand nand_2 (nand_2_out, Clock, not_1_out);
  nand nand_3 (Q, nand_1_out, nand_4_out);
  nand nand_4 (nand_4_out, Q, nand_2_out);
endmodule
