// Digital circuit 4-bit_register.dig as structural Verilog
module _4_bit_register (
  input  [3:0] Data,
  input  Clock,
  input  Clear,
  input  R_W,
  output [3:0] Out
);

  wire and_1_out;
  wire [3:0] and_2_out;
  wire [3:3] not_1_out;

  not not_1 (not_1_out[3], Clear);
  and and_1 (and_1_out, R_W, Clock);
  assign and_2_out = Data & {4{not_1_out[3]}};  // And and_2, 4 bits wide
  D_FF d_ff_1 (.D(and_2_out[0]), .C(and_1_out), .Q(Out[0]));  // open: nQ
  D_FF d_ff_2 (.D(and_2_out[1]), .C(and_1_out), .Q(Out[1]));  // open: nQ
  D_FF d_ff_3 (.D(and_2_out[2]), .C(and_1_out), .Q(Out[2]));  // open: nQ
  D_FF d_ff_4 (.D(and_2_out[3]), .C(and_1_out), .Q(Out[3]));  // open: nQ
endmodule
