// Digital circuit 4bit_registerFileALU.dig as structural Verilog
module _4bit_registerFileALU (
  input  [3:0] Write_Register,
  input  [3:0] Read_Register_1,
  input  [3:0] Read_Register_2,
  input  [3:0] Write_Data,
  input  Clock,
  output [3:0] Read_Data_1,
  output [3:0] Read_data_2
);

  wire [3:0] _4_bit_register_1_out, _4_bit_register_2_out, _4_bit_register_3_out, _4_bit_register_4_out,
       demultiplexer_1_out_0, demultiplexer_1_out_1, demultiplexer_1_out_2, demultiplexer_1_out_3;

  Demultiplexer #(.Bits(4), .Selector_Bits(2)) demultiplexer_1 (
    .sel(Write_Register[1:0]), .in(Write_Data), .out_0(demultiplexer_1_out_0), .out_1(demultiplexer_1_out_1),
    .out_2(demultiplexer_1_out_2), .out_3(demultiplexer_1_out_3));
  _4_bit_register _4_bit_register_1 (
    .Data(demultiplexer_1_out_0), .Clear(Clock), .Out(_4_bit_register_1_out));  // open: Clock
  _4_bit_register _4_bit_register_2 (
    .Data(demultiplexer_1_out_1), .Clear(Clock), .Out(_4_bit_register_2_out));  // open: Clock
  _4_bit_register _4_bit_register_3 (
    .Data(demultiplexer_1_out_2), .Clear(Clock), .Out(_4_bit_register_3_out));  // open: Clock
  _4_bit_register _4_bit_register_4 (
    .Data(demultiplexer_1_out_3), .Clear(Clock), .Out(_4_bit_register_4_out));  // open: Clock
  Multiplexer #(.Bits(4), .Selector_Bits(2)) multiplexer_1 (
    .sel(Read_Register_1[1:0]), .in_0(_4_bit_register_1_out), .in_1(_4_bit_register_2_out),
    .in_2(_4_bit_register_3_out), .in_3(_4_bit_register_4_out), .out(Read_Data_1));
  Multiplexer #(.Bits(4), .Selector_Bits(2)) multiplexer_2 (
    .sel(Read_Register_2[1:0]), .in_0(_4_bit_register_1_out), .in_1(_4_bit_register_2_out),
    .in_2(_4_bit_register_3_out), .in_3(_4_bit_register_4_out), .out(Read_data_2));
  // Pins of 2 and 4 bits meet at Write_Register
  // Pins of 2 and 4 bits meet at Read_Register_1
  // Pins of 2 and 4 bits meet at Read_Register_2
endmodule
