// Digital circuit CU.dig as structural Verilog
module CU (
  input  [3:0] Opcode__IR,
  input  Zero_flag,
  input  reset,
  input  clock,
  output [2:0] ALU_Op,
  output [1:0] Read_Reg_1,
  output [1:0] Read_Reg_2,
  output [1:0] Write_Reg,
  output Write_Enabled,
  output Immediate_Load,
  output Increment,
  output Fetch_Enable,
  output Zero_Flag_2
);

  wire and_3_out, and_4_out, and_5_out, and_6_out, finitestatemachine_1_msb, not_2_out, not_3_out, not_4_out,
       not_5_out, not_6_out, not_7_out, not_8_out, not_9_out, not_10_out, not_11_out, not_12_out, not_13_out,
       not_14_out, not_15_out, not_16_out, not_17_out, not_18_out, not_19_out, not_20_out, not_22_out,
       not_23_out, not_24_out, not_25_out, not_26_out, not_27_out, not_28_out, not_29_out, or_1_out, or_4_out;
  wire [0:0] not_21_out, or_2_out, or_3_out;
  wire [2:0] and_13_out, and_14_out, and_15_out, and_16_out, and_17_out, and_18_out, xor_1_out, xor_2_out;
  wire [2:2] and_7_out, and_8_out, and_9_out, and_10_out, and_11_out, and_12_out, and_24_out;
  wire [3:0] and_1_out, and_2_out;
  wire [3:3] finitestatemachine_1_lsb, not_1_out;

  assign and_1_out = {4{finitestatemachine_1_lsb[3]}} & Opcode__IR;  // And and_1, 4 bits wide
  not not_1 (not_1_out[3], reset);
  assign and_2_out = and_1_out & {4{not_1_out[3]}} & {4{clock}};  // And and_2, 4 bits wide
  not not_2 (not_2_out, and_2_out[2]);
  not not_3 (not_3_out, and_2_out[3]);
  not not_4 (not_4_out, and_2_out[1]);
  not not_5 (not_5_out, and_2_out[0]);
  not not_6 (not_6_out, and_2_out[2]);
  not not_7 (not_7_out, and_2_out[1]);
  not not_8 (not_8_out, and_2_out[3]);
  not not_9 (not_9_out, and_2_out[0]);
  not not_10 (not_10_out, and_2_out[3]);
  not not_11 (not_11_out, and_2_out[0]);
  and and_3 (and_3_out, not_11_out, and_2_out[1], not_2_out, not_3_out);
  and and_4 (and_4_out, not_4_out, not_5_out, not_6_out);
  or or_1 (or_1_out, and_2_out[0], and_2_out[1], and_2_out[2], and_2_out[3]);
  and and_5 (and_5_out, and_2_out[0], not_7_out, not_8_out);
  and and_6 (and_6_out, not_9_out, and_2_out[1], not_10_out);
  or or_2 (or_2_out[0], and_2_out[0], and_2_out[1], and_2_out[2], and_2_out[3]);
  not not_12 (not_12_out, and_2_out[1]);
  not not_13 (not_13_out, and_2_out[2]);
  not not_14 (not_14_out, and_2_out[0]);
  not not_15 (not_15_out, and_2_out[2]);
  not not_16 (not_16_out, and_2_out[2]);
  not not_17 (not_17_out, and_2_out[0]);
  not not_18 (not_18_out, and_2_out[1]);
  not not_19 (not_19_out, and_2_out[1]);
  not not_20 (not_20_out, and_2_out[0]);
  or or_3 (or_3_out[0], and_3_out, and_4_out);
  or or_4 (or_4_out, and_5_out, and_6_out);
  and and_7 (and_7_out[2], and_2_out[0], not_12_out, not_13_out, and_2_out[3]);
  and and_8 (and_8_out[2], not_14_out, and_2_out[1], not_15_out, and_2_out[3]);
  and and_9 (and_9_out[2], and_2_out[0], and_2_out[1], not_16_out, and_2_out[3]);
  and and_10 (and_10_out[2], not_17_out, not_18_out, and_2_out[2], and_2_out[3]);
  and and_11 (and_11_out[2], and_2_out[0], not_19_out, and_2_out[2], and_2_out[3]);
  and and_12 (and_12_out[2], not_20_out, and_2_out[1], and_2_out[2], and_2_out[3]);
  not not_21 (not_21_out[0], and_2_out[3]);
  assign and_13_out = 3'b000 & {3{and_7_out[2]}};  // And and_13, 3 bits wide
  assign and_14_out = 3'b001 & {3{and_8_out[2]}};  // And and_14, 3 bits wide
  assign and_15_out = 3'b010 & {3{and_9_out[2]}};  // And and_15, 3 bits wide
  assign and_16_out = 3'b011 & {3{and_10_out[2]}};  // And and_16, 3 bits wide
  assign and_17_out = 3'b100 & {3{and_11_out[2]}};  // And and_17, 3 bits wide
  assign and_18_out = 3'b101 & {3{and_12_out[2]}};  // And and_18, 3 bits wide
  assign Write_Reg = {2{finitestatemachine_1_lsb[3]}} & {1'b0, or_3_out[0]};  // And and_19, 2 bits wide
  and and_20 (Write_Enabled, or_1_out, finitestatemachine_1_lsb[3]);
  assign Read_Reg_1 = {1'b0, not_21_out[0]} & {2{finitestatemachine_1_lsb[3]}};  // And and_21, 2 bits wide
  assign Read_Reg_2 = {1'b0, or_2_out[0]} & {2{finitestatemachine_1_lsb[3]}};  // And and_22, 2 bits wide
  finiteStateMachine finitestatemachine_1 (
    .Input(1'b1), .Clock(clock), .MSB(finitestatemachine_1_msb), .LSB(finitestatemachine_1_lsb[3]));
  assign xor_1_out = and_13_out ^ and_14_out ^ and_15_out ^ and_16_out ^ and_17_out ^ and_18_out;  // XOr xor_1, 3 bits wide
  and and_23 (Immediate_Load, finitestatemachine_1_lsb[3], or_4_out);
  not not_22 (not_22_out, and_7_out[2]);
  not not_23 (not_23_out, and_8_out[2]);
  not not_24 (not_24_out, and_9_out[2]);
  not not_25 (not_25_out, and_10_out[2]);
  not not_26 (not_26_out, and_11_out[2]);
  not not_27 (not_27_out, and_12_out[2]);
  and and_24 (and_24_out[2], not_22_out, not_23_out, not_24_out, not_25_out, not_26_out, not_27_out);
  and and_25 (Fetch_Enable, not_28_out, not_29_out);
  not not_28 (not_28_out, finitestatemachine_1_msb);
  not not_29 (not_29_out, finitestatemachine_1_lsb[3]);
  assign xor_2_out = xor_1_out ^ {3{and_24_out[2]}};  // XOr xor_2, 3 bits wide
  assign ALU_Op = {3{finitestatemachine_1_lsb[3]}} & xor_2_out;  // And and_26, 3 bits wide

  assign Increment = Fetch_Enable;
  assign Zero_Flag_2 = Zero_flag;
endmodule
