// Digital circuit part1_steps3&4_(programCounter&IR).dig as structural Verilog
module part1_steps3_4__programCounter_IR (
  input  increment,
  input  clk,
  input  [3:0] Address,
  output [3:0] DataOut__To_CU,
  output reset_flag
);

  wire [3:0] memory_module_1_data_2, programcounter_1_address_bus;

  programCounter programcounter_1 (
    .Load(Address), .Increment(increment), .Address_bus(programcounter_1_address_bus),
    .Out_of_range(reset_flag));  // open: Clock, R_W, Clear
  memory_Module memory_module_1 (
    .Address(programcounter_1_address_bus), .clock(clk), .data_2(memory_module_1_data_2));  // open: Data, Read, Write
  _4bit_Instruction_Register _4bit_instruction_register_1 (
    .Data(memory_module_1_data_2), .Clock(clk), .Address_Bus(DataOut__To_CU));  // open: Clear, R_W, ALU_Op
endmodule
